# Fritzing sketch Light and temp sensor (saved by Fritzing 1.0.5)
breadboards: 1

parts:
  R1 = Resistor [tolerance=±5% power=0.25W resistance=10k package=THT]
  J1 = female pin header, 15 pins [form="♀ (female)"]
  J2 = female pin header, 15 pins [form="♀ (female)"]
  RHT1 = Humidity and Temperature Sensor RHT03
  R2 = Photocell (LDR) [power=0.25W dark_resistance_@0.01lx=300kΩ light_resistance_@100lx=400Ω luminance=10lx package=THT]
  R3 = Resistor [tolerance=±5% power=0.25W resistance=220 package=THT]

nets:
  N1: R1.Pin_0, J2.pin10, R2.pin_1
  N2: R1.Pin_1, J1.pin2, RHT1.GND_2
  N3: J1.pin1, RHT1.Vcc, R2.pin_0, R3.Pin_1
  N4: J1.pin5, RHT1.Data-signal, R3.Pin_0

notes:
  VIN, GND, D13, D12, D14, D27, D26, D25, D33, D32, D35, D34, VN, VP, GV
  3V3, GND, D15, D2, D4, D16, D17, D5, D18, D19, D21, RX0, TX0, D22, D23
